// Logisim project bt23cse126assig.circ as structural Verilog: 10 circuits, main circuit CALULATOR
module CALULATOR (
  input  [7:0] in_1,
  input  [7:0] in_2,
  input  [1:0] SELECT_LINE,
  output [15:0] A0
);

  wire binarytohexa_1_out_2, binarytohexa_1_out_3, binarytohexa_1_out_4, binarytohexa_1_out_5,
       binarytohexa_1_out_6, binarytohexa_1_out_7, binarytohexa_1_out_8, binarytohexa_2_out_2,
       binarytohexa_2_out_3, binarytohexa_2_out_4, binarytohexa_2_out_5, binarytohexa_2_out_6,
       binarytohexa_2_out_7, binarytohexa_2_out_8, binarytohexa_3_out_2, binarytohexa_3_out_3,
       binarytohexa_3_out_4, binarytohexa_3_out_5, binarytohexa_3_out_6, binarytohexa_3_out_7,
       binarytohexa_3_out_8, binarytohexa_4_out_2, binarytohexa_4_out_3, binarytohexa_4_out_4,
       binarytohexa_4_out_5, binarytohexa_4_out_6, binarytohexa_4_out_7, binarytohexa_4_out_8;
  wire [8:0] n8bit_adderorsub_2_s0;
  wire [9:0] n8bit_adderorsub_1_s0;
  wire [15:0] n8bitdivider_1_r0, n8bitmultiplier_1_s0;

  _8bitMULTIPLIER u_8bitmultiplier_1 (
    .in_1(1'b1), .L(in_1), .L_2(in_2), .S0(n8bitmultiplier_1_s0[0]), .S1(n8bitmultiplier_1_s0[1]),
    .S2(n8bitmultiplier_1_s0[2]), .S3(n8bitmultiplier_1_s0[3]), .S4(n8bitmultiplier_1_s0[4]),
    .S5(n8bitmultiplier_1_s0[5]), .S6(n8bitmultiplier_1_s0[6]), .S7(n8bitmultiplier_1_s0[7]),
    .S8(n8bitmultiplier_1_s0[8]), .S9(n8bitmultiplier_1_s0[9]), .S10(n8bitmultiplier_1_s0[10]),
    .S11(n8bitmultiplier_1_s0[11]), .S12(n8bitmultiplier_1_s0[12]), .S13(n8bitmultiplier_1_s0[13]),
    .S14(n8bitmultiplier_1_s0[14]), .S15(n8bitmultiplier_1_s0[15]));
  _8BITDIVIDER u_8bitdivider_1 (
    .in_3(1'b1), .in_1(in_1), .in_2(in_2), .Q7(n8bitdivider_1_r0[15]), .Q6(n8bitdivider_1_r0[14]),
    .Q5(n8bitdivider_1_r0[13]), .Q4(n8bitdivider_1_r0[12]), .Q3(n8bitdivider_1_r0[11]),
    .Q2(n8bitdivider_1_r0[10]), .Q1(n8bitdivider_1_r0[9]), .Q0(n8bitdivider_1_r0[8]),
    .R7(n8bitdivider_1_r0[7]), .R6(n8bitdivider_1_r0[6]), .out_13(n8bitdivider_1_r0[5]),
    .out_14(n8bitdivider_1_r0[4]), .out_15(n8bitdivider_1_r0[3]), .R1(n8bitdivider_1_r0[2]),
    .out_17(n8bitdivider_1_r0[1]), .R0(n8bitdivider_1_r0[0]));
  _8bit_adderorSub u_8bit_adderorsub_1 (
    .L(in_1), .in_3(in_2), .Cntrl(1'b0), .S0(n8bit_adderorsub_1_s0[0]), .S1(n8bit_adderorsub_1_s0[1]),
    .S2(n8bit_adderorsub_1_s0[2]), .S3(n8bit_adderorsub_1_s0[3]), .S4(n8bit_adderorsub_1_s0[4]),
    .S5(n8bit_adderorsub_1_s0[5]), .S6(n8bit_adderorsub_1_s0[6]), .out_13(n8bit_adderorsub_1_s0[7]),
    .out_14(n8bit_adderorsub_1_s0[8]), .S7(n8bit_adderorsub_1_s0[9]), .in_1(1'b1));
  _8bit_adderorSub u_8bit_adderorsub_2 (
    .L(in_2), .in_3(in_1), .Cntrl(1'b1), .S0(n8bit_adderorsub_2_s0[0]), .S1(n8bit_adderorsub_2_s0[1]),
    .S2(n8bit_adderorsub_2_s0[2]), .S3(n8bit_adderorsub_2_s0[3]), .S4(n8bit_adderorsub_2_s0[4]),
    .S5(n8bit_adderorsub_2_s0[5]), .S6(n8bit_adderorsub_2_s0[6]), .out_13(n8bit_adderorsub_2_s0[7]),
    .out_14(n8bit_adderorsub_2_s0[8]), .in_1(1'b1));  // open: S7
  Multiplexer #(.select(2), .width(16)) multiplexer_1 (
    .in0({{6{1'b0}}, n8bit_adderorsub_1_s0}), .in1({{7{1'b0}}, n8bit_adderorsub_2_s0}),
    .in2(n8bitmultiplier_1_s0), .in3(n8bitdivider_1_r0), .out(A0), .sel(SELECT_LINE), .en(1'b1));
  _7_Segment_Display u_7_segment_display_1 (
    .g(binarytohexa_1_out_8), .f(binarytohexa_1_out_6), .a(binarytohexa_1_out_7), .b(binarytohexa_1_out_2),
    .e(binarytohexa_1_out_5), .d(binarytohexa_1_out_4), .c(binarytohexa_1_out_3));  // open: dp
  binarytohexa binarytohexa_1 (
    .out_2(binarytohexa_1_out_2), .out_3(binarytohexa_1_out_3), .out_4(binarytohexa_1_out_4),
    .out_5(binarytohexa_1_out_5), .out_6(binarytohexa_1_out_6), .out_7(binarytohexa_1_out_7),
    .out_8(binarytohexa_1_out_8), .in_1(A0[15:12]));
  _7_Segment_Display u_7_segment_display_2 (
    .g(binarytohexa_2_out_8), .f(binarytohexa_2_out_6), .a(binarytohexa_2_out_7), .b(binarytohexa_2_out_2),
    .e(binarytohexa_2_out_5), .d(binarytohexa_2_out_4), .c(binarytohexa_2_out_3));  // open: dp
  binarytohexa binarytohexa_2 (
    .out_2(binarytohexa_2_out_2), .out_3(binarytohexa_2_out_3), .out_4(binarytohexa_2_out_4),
    .out_5(binarytohexa_2_out_5), .out_6(binarytohexa_2_out_6), .out_7(binarytohexa_2_out_7),
    .out_8(binarytohexa_2_out_8), .in_1(A0[11:8]));
  binarytohexa binarytohexa_3 (
    .out_2(binarytohexa_3_out_2), .out_3(binarytohexa_3_out_3), .out_4(binarytohexa_3_out_4),
    .out_5(binarytohexa_3_out_5), .out_6(binarytohexa_3_out_6), .out_7(binarytohexa_3_out_7),
    .out_8(binarytohexa_3_out_8), .in_1(A0[7:4]));
  _7_Segment_Display u_7_segment_display_3 (
    .g(binarytohexa_3_out_8), .f(binarytohexa_3_out_6), .a(binarytohexa_3_out_7), .b(binarytohexa_3_out_2),
    .e(binarytohexa_3_out_5), .d(binarytohexa_3_out_4), .c(binarytohexa_3_out_3));  // open: dp
  _7_Segment_Display u_7_segment_display_4 (
    .g(binarytohexa_4_out_8), .f(binarytohexa_4_out_6), .a(binarytohexa_4_out_7), .b(binarytohexa_4_out_2),
    .e(binarytohexa_4_out_5), .d(binarytohexa_4_out_4), .c(binarytohexa_4_out_3));  // open: dp
  binarytohexa binarytohexa_4 (
    .out_2(binarytohexa_4_out_2), .out_3(binarytohexa_4_out_3), .out_4(binarytohexa_4_out_4),
    .out_5(binarytohexa_4_out_5), .out_6(binarytohexa_4_out_6), .out_7(binarytohexa_4_out_7),
    .out_8(binarytohexa_4_out_8), .in_1(A0[3:0]));

  // Other names for the same wires on the sheet: A0_t = in_1[0]; A1 = in_1[1]; A2 = in_1[2]; A3 = in_1[3];
  //   A4 = in_1[4]; A5 = in_1[5]; A6 = in_1[6]; A7 = in_1[7]; B0 = in_2[0]; B1 = in_2[1]; B2 = in_2[2]; B3 = in_2[3];
  //   B4 = in_2[4]; B5 = in_2[5]; B6 = in_2[6]; B7 = in_2[7]

  // Notes on the sheet:
  //   REMAINDER
  //   R0
  //   R7
  //   Q0
  //   Q8
  //   OUTPUT(binary)
  //   A15
  //   DIVISION BY ZERO UNDEFINED
  //   ARITHMETIC CALCULATOR
  //   Q
  //   R
  //   SIGN 1=+VE 0=-VE
  //   00 FOR ADD
  //   01 FOR SUBTRACT
  //   Q1
  //   M3
  //   SIGN
  //   10 FOR MULTIPLICATION
  //   11 FOR DIVISION
  //   Q0
  //   M2
  //   SIGN
  //   CARRY
  //   OUTPUT
  //   R1
  //   M1
  //   D1
  //   S1
  //   R0
  //   M0
  //   D0
  //   S0
  //   DIV
  //   MUL
  //   SUB
  //   ADD
endmodule

module _1bitadder (
  input  CIN,
  input  A,
  input  B,
  input  EN,
  input  in_5,
  input  in_6,
  output out_7,
  output out_8
);

  wire not_1_out;

  not not_1 (not_1_out, CIN);
  Multiplexer #(.select(2)) multiplexer_1 (
    .in0(CIN), .in1(not_1_out), .in2(not_1_out), .in3(CIN), .out(out_7), .sel({A, B}), .en(EN));
  Multiplexer #(.select(2)) multiplexer_2 (
    .in0(in_5), .in1(CIN), .in2(CIN), .in3(in_6), .out(out_8), .sel({A, B}), .en(EN));

  // Notes on the sheet:
  //   8bit adder
endmodule

module _8BITADDER (
  input  CIN,
  input  A0,
  input  B0,
  input  A1,
  input  B1,
  input  A2,
  input  B2,
  input  A3,
  input  B3,
  input  A4,
  input  B4,
  input  A5,
  input  B5,
  input  A6,
  input  B6,
  input  A7,
  input  B7,
  input  in_18,
  input  in_19,
  input  in_20,
  output S0,
  output S1,
  output S2,
  output S3,
  output S4,
  output S5,
  output S6,
  output S7,
  output S8_COUT
);

  wire n1bitadder_1_out_8, n1bitadder_2_out_8, n1bitadder_3_out_8, n1bitadder_4_out_8, n1bitadder_5_out_8,
       n1bitadder_6_out_8, n1bitadder_7_out_8;

  _1bitadder u_1bitadder_1 (
    .CIN(CIN), .A(A0), .B(B0), .EN(in_18), .in_5(in_19), .in_6(in_20), .out_7(S0), .out_8(n1bitadder_1_out_8));
  _1bitadder u_1bitadder_2 (
    .CIN(n1bitadder_1_out_8), .A(A1), .B(B1), .EN(in_18), .in_5(in_19), .in_6(in_20), .out_7(S1),
    .out_8(n1bitadder_2_out_8));
  _1bitadder u_1bitadder_3 (
    .CIN(n1bitadder_2_out_8), .A(A2), .B(B2), .EN(in_18), .in_5(in_19), .in_6(in_20), .out_7(S2),
    .out_8(n1bitadder_3_out_8));
  _1bitadder u_1bitadder_4 (
    .CIN(n1bitadder_3_out_8), .A(A3), .B(B3), .EN(in_18), .in_5(in_19), .in_6(in_20), .out_7(S3),
    .out_8(n1bitadder_4_out_8));
  _1bitadder u_1bitadder_5 (
    .CIN(n1bitadder_4_out_8), .A(A4), .B(B4), .EN(in_18), .in_5(in_19), .in_6(in_20), .out_7(S4),
    .out_8(n1bitadder_5_out_8));
  _1bitadder u_1bitadder_6 (
    .CIN(n1bitadder_5_out_8), .A(A5), .B(B5), .EN(in_18), .in_5(in_19), .in_6(in_20), .out_7(S5),
    .out_8(n1bitadder_6_out_8));
  _1bitadder u_1bitadder_7 (
    .CIN(n1bitadder_6_out_8), .A(A6), .B(B6), .EN(in_18), .in_5(in_19), .in_6(in_20), .out_7(S6),
    .out_8(n1bitadder_7_out_8));
  _1bitadder u_1bitadder_8 (
    .CIN(n1bitadder_7_out_8), .A(A7), .B(B7), .EN(in_18), .in_5(in_19), .in_6(in_20), .out_7(S7),
    .out_8(S8_COUT));

  // Notes on the sheet:
  //   B
  //   0
  //   A
  //   E
  //   C1
  //   0
  //   B
  //   C1
  //   E
  //   A
  //   CIN
  //   B
  //   A
  //   CIN
  //   0
  //   C1
  //   E
  //   CIN
  //   C0
  //   B
  //   E
  //   A
  //   C1
  //   B
  //   A
  //   E
  //   CIN
  //   0
  //   C1
  //   CIN
  //   B
  //   0
  //   E
  //   A
  //   C1
  //   CIN
  //   0
  //   B
  //   A
  //   C1
  //   E
  //   CIN
  //   0
  //   B
  //   A
  //   E
  //   C1
  //   8BIT ADDER
endmodule

module _8bitMULTIPLIER (
  input  in_1,
  input  [7:0] L,
  input  [7:0] L_2,
  output S0,
  output S1,
  output S2,
  output S3,
  output S4,
  output S5,
  output S6,
  output S7,
  output S8,
  output S9,
  output S10,
  output S11,
  output S12,
  output S13,
  output S14,
  output S15
);

  wire _0_2_out, _0_3_out, _0_4_out, _0_5_out, _0_6_out, _0_7_out, _0_out, _1_2_out, _1_3_out, _1_4_out,
       _1_5_out, _1_6_out, _1_7_out, _1_8_out, _1_out, _2_2_out, _2_3_out, _2_4_out, _2_5_out, _2_6_out,
       _2_7_out, _2_8_out, _2_out, _3_2_out, _3_3_out, _3_4_out, _3_5_out, _3_6_out, _3_7_out, _3_8_out,
       _3_out, _4_2_out, _4_3_out, _4_4_out, _4_5_out, _4_6_out, _4_7_out, _4_8_out, _4_out, _5_2_out,
       _5_3_out, _5_4_out, _5_5_out, _5_6_out, _5_7_out, _5_8_out, _5_out, _6_2_out, _6_3_out, _6_4_out,
       _6_5_out, _6_6_out, _6_7_out, _6_8_out, _6_out, _7_2_out, _7_3_out, _7_4_out, _7_5_out, _7_6_out,
       _7_7_out, _7_8_out, _7_out, n8bitadder_1_s1, n8bitadder_1_s2, n8bitadder_1_s3, n8bitadder_1_s4,
       n8bitadder_1_s5, n8bitadder_1_s6, n8bitadder_1_s7, n8bitadder_1_s8_cout, n8bitadder_3_s1,
       n8bitadder_3_s2, n8bitadder_3_s3, n8bitadder_3_s4, n8bitadder_3_s5, n8bitadder_3_s6, n8bitadder_3_s7,
       n8bitadder_3_s8_cout, n8bitadder_4_s1, n8bitadder_4_s2, n8bitadder_4_s3, n8bitadder_4_s4,
       n8bitadder_4_s5, n8bitadder_4_s6, n8bitadder_4_s7, n8bitadder_4_s8_cout, n8bitadder_5_s1,
       n8bitadder_5_s2, n8bitadder_5_s3, n8bitadder_5_s4, n8bitadder_5_s5, n8bitadder_5_s6, n8bitadder_5_s7,
       n8bitadder_5_s8_cout, n8bitadder_6_s1, n8bitadder_6_s2, n8bitadder_6_s3, n8bitadder_6_s4,
       n8bitadder_6_s5, n8bitadder_6_s6, n8bitadder_6_s7, n8bitadder_6_s8_cout, n8bitadder_7_s1,
       n8bitadder_7_s2, n8bitadder_7_s3, n8bitadder_7_s4, n8bitadder_7_s5, n8bitadder_7_s6, n8bitadder_7_s7,
       n8bitadder_7_s8_cout;

  and _7 (_7_out, L_2[7], L[7]);
  and _6 (_6_out, L_2[6], L[6]);
  and _7_2 (_7_2_out, L_2[6], L[7]);
  and _5 (_5_out, L_2[7], L[5]);
  and _6_2 (_6_2_out, L_2[7], L[6]);
  and _4 (_4_out, L_2[7], L[4]);
  and _7_3 (_7_3_out, L_2[4], L[7]);
  and _7_4 (_7_4_out, L_2[5], L[7]);
  and _6_3 (_6_3_out, L_2[5], L[6]);
  and _5_2 (_5_2_out, L_2[5], L[5]);
  and _4_2 (_4_2_out, L_2[6], L[4]);
  and _5_3 (_5_3_out, L_2[6], L[5]);
  and _3 (_3_out, L_2[7], L[3]);
  and _2 (_2_out, L_2[7], L[2]);
  and _7_5 (_7_5_out, L_2[3], L[7]);
  and _5_4 (_5_4_out, L_2[4], L[5]);
  and _6_4 (_6_4_out, L_2[4], L[6]);
  and _4_3 (_4_3_out, L_2[5], L[4]);
  and _3_2 (_3_2_out, L_2[5], L[3]);
  and _2_2 (_2_2_out, L_2[5], L[2]);
  and _2_3 (_2_3_out, L_2[6], L[2]);
  and _1 (_1_out, L_2[6], L[1]);
  and _3_3 (_3_3_out, L_2[6], L[3]);
  and _1_2 (_1_2_out, L_2[7], L[1]);
  and _0 (_0_out, L_2[7], L[0]);
  and _6_5 (_6_5_out, L_2[2], L[6]);
  and _7_6 (_7_6_out, L_2[2], L[7]);
  and _5_5 (_5_5_out, L_2[3], L[5]);
  and _4_4 (_4_4_out, L_2[3], L[4]);
  and _6_6 (_6_6_out, L_2[3], L[6]);
  and _4_5 (_4_5_out, L_2[4], L[4]);
  and _2_4 (_2_4_out, L_2[4], L[2]);
  and _3_4 (_3_4_out, L_2[4], L[3]);
  and _0_2 (_0_2_out, L_2[5], L[0]);
  and _1_3 (_1_3_out, L_2[5], L[1]);
  and _0_3 (_0_3_out, L_2[6], L[0]);
  and _7_7 (_7_7_out, L_2[1], L[7]);
  and _3_5 (_3_5_out, L_2[2], L[3]);
  and _4_6 (_4_6_out, L_2[2], L[4]);
  and _5_6 (_5_6_out, L_2[2], L[5]);
  and _1_4 (_1_4_out, L_2[3], L[1]);
  and _3_6 (_3_6_out, L_2[3], L[3]);
  and _2_5 (_2_5_out, L_2[3], L[2]);
  and _1_5 (_1_5_out, L_2[4], L[1]);
  and _0_4 (_0_4_out, L_2[4], L[0]);
  _8BITADDER u_8bitadder_1 (
    .CIN(1'b0), .S0(S6), .S1(n8bitadder_1_s1), .S2(n8bitadder_1_s2), .S3(n8bitadder_1_s3),
    .S4(n8bitadder_1_s4), .S5(n8bitadder_1_s5), .S6(n8bitadder_1_s6), .S7(n8bitadder_1_s7),
    .S8_COUT(n8bitadder_1_s8_cout), .A0(n8bitadder_3_s1), .B0(_0_3_out), .in_18(in_1), .in_19(1'b0),
    .in_20(1'b1), .A1(n8bitadder_3_s2), .B1(_1_out), .A2(n8bitadder_3_s3), .B2(_2_3_out),
    .A3(n8bitadder_3_s4), .B3(_3_3_out), .A4(n8bitadder_3_s5), .B4(_4_2_out), .A5(n8bitadder_3_s6),
    .B5(_5_3_out), .A6(n8bitadder_3_s7), .B6(_6_out), .A7(n8bitadder_3_s8_cout), .B7(_7_2_out));
  _8BITADDER u_8bitadder_2 (
    .CIN(1'b0), .S0(S7), .S1(S8), .S2(S9), .S3(S10), .S4(S11), .S5(S12), .S6(S13), .S7(S14), .S8_COUT(S15),
    .A0(n8bitadder_1_s1), .B0(_0_out), .in_18(in_1), .in_19(1'b0), .in_20(1'b1), .A1(n8bitadder_1_s2),
    .B1(_1_2_out), .A2(n8bitadder_1_s3), .B2(_2_out), .A3(n8bitadder_1_s4), .B3(_3_out),
    .A4(n8bitadder_1_s5), .B4(_4_out), .A5(n8bitadder_1_s6), .B5(_5_out), .A6(n8bitadder_1_s7),
    .B6(_6_2_out), .A7(n8bitadder_1_s8_cout), .B7(_7_out));
  and _5_7 (_5_7_out, L_2[1], L[5]);
  and _6_7 (_6_7_out, L_2[1], L[6]);
  and _1_6 (_1_6_out, L_2[2], L[1]);
  and _0_5 (_0_5_out, L_2[2], L[0]);
  and _2_6 (_2_6_out, L_2[2], L[2]);
  and _0_6 (_0_6_out, L_2[3], L[0]);
  _8BITADDER u_8bitadder_3 (
    .CIN(1'b0), .S0(S5), .S1(n8bitadder_3_s1), .S2(n8bitadder_3_s2), .S3(n8bitadder_3_s3),
    .S4(n8bitadder_3_s4), .S5(n8bitadder_3_s5), .S6(n8bitadder_3_s6), .S7(n8bitadder_3_s7),
    .S8_COUT(n8bitadder_3_s8_cout), .A0(n8bitadder_4_s1), .B0(_0_2_out), .in_18(in_1), .in_19(1'b0),
    .in_20(1'b1), .A1(n8bitadder_4_s2), .B1(_1_3_out), .A2(n8bitadder_4_s3), .B2(_2_2_out),
    .A3(n8bitadder_4_s4), .B3(_3_2_out), .A4(n8bitadder_4_s5), .B4(_4_3_out), .A5(n8bitadder_4_s6),
    .B5(_5_2_out), .A6(n8bitadder_4_s7), .B6(_6_3_out), .A7(n8bitadder_4_s8_cout), .B7(_7_4_out));
  and _2_7 (_2_7_out, L_2[1], L[2]);
  and _4_7 (_4_7_out, L_2[1], L[4]);
  and _3_7 (_3_7_out, L_2[1], L[3]);
  _8BITADDER u_8bitadder_4 (
    .CIN(1'b0), .S0(S4), .S1(n8bitadder_4_s1), .S2(n8bitadder_4_s2), .S3(n8bitadder_4_s3),
    .S4(n8bitadder_4_s4), .S5(n8bitadder_4_s5), .S6(n8bitadder_4_s6), .S7(n8bitadder_4_s7),
    .S8_COUT(n8bitadder_4_s8_cout), .A0(n8bitadder_6_s1), .B0(_0_4_out), .in_18(in_1), .in_19(1'b0),
    .in_20(1'b1), .A1(n8bitadder_6_s2), .B1(_1_5_out), .A2(n8bitadder_6_s3), .B2(_2_4_out),
    .A3(n8bitadder_6_s4), .B3(_3_4_out), .A4(n8bitadder_6_s5), .B4(_4_5_out), .A5(n8bitadder_6_s6),
    .B5(_5_4_out), .A6(n8bitadder_6_s7), .B6(_6_4_out), .A7(n8bitadder_6_s8_cout), .B7(_7_3_out));
  and _7_8 (_7_8_out, L_2[0], L[7]);
  and _0_7 (_0_7_out, L_2[1], L[0]);
  and _1_7 (_1_7_out, L_2[1], L[1]);
  _8BITADDER u_8bitadder_5 (
    .CIN(1'b0), .S0(S2), .S1(n8bitadder_5_s1), .S2(n8bitadder_5_s2), .S3(n8bitadder_5_s3),
    .S4(n8bitadder_5_s4), .S5(n8bitadder_5_s5), .S6(n8bitadder_5_s6), .S7(n8bitadder_5_s7),
    .S8_COUT(n8bitadder_5_s8_cout), .A0(n8bitadder_7_s1), .B0(_0_5_out), .in_18(in_1), .in_19(1'b0),
    .in_20(1'b1), .A1(n8bitadder_7_s2), .B1(_1_6_out), .A2(n8bitadder_7_s3), .B2(_2_6_out),
    .A3(n8bitadder_7_s4), .B3(_3_5_out), .A4(n8bitadder_7_s5), .B4(_4_6_out), .A5(n8bitadder_7_s6),
    .B5(_5_6_out), .A6(n8bitadder_7_s7), .B6(_6_5_out), .A7(n8bitadder_7_s8_cout), .B7(_7_6_out));
  _8BITADDER u_8bitadder_6 (
    .CIN(1'b0), .S0(S3), .S1(n8bitadder_6_s1), .S2(n8bitadder_6_s2), .S3(n8bitadder_6_s3),
    .S4(n8bitadder_6_s4), .S5(n8bitadder_6_s5), .S6(n8bitadder_6_s6), .S7(n8bitadder_6_s7),
    .S8_COUT(n8bitadder_6_s8_cout), .A0(n8bitadder_5_s1), .B0(_0_6_out), .in_18(in_1), .in_19(1'b0),
    .in_20(1'b1), .A1(n8bitadder_5_s2), .B1(_1_4_out), .A2(n8bitadder_5_s3), .B2(_2_5_out),
    .A3(n8bitadder_5_s4), .B3(_3_6_out), .A4(n8bitadder_5_s5), .B4(_4_4_out), .A5(n8bitadder_5_s6),
    .B5(_5_5_out), .A6(n8bitadder_5_s7), .B6(_6_6_out), .A7(n8bitadder_5_s8_cout), .B7(_7_5_out));
  and _6_8 (_6_8_out, L_2[0], L[6]);
  and _5_8 (_5_8_out, L_2[0], L[5]);
  and _4_8 (_4_8_out, L_2[0], L[4]);
  and _2_8 (_2_8_out, L_2[0], L[2]);
  and _3_8 (_3_8_out, L_2[0], L[3]);
  _8BITADDER u_8bitadder_7 (
    .CIN(1'b0), .S0(S1), .S1(n8bitadder_7_s1), .S2(n8bitadder_7_s2), .S3(n8bitadder_7_s3),
    .S4(n8bitadder_7_s4), .S5(n8bitadder_7_s5), .S6(n8bitadder_7_s6), .S7(n8bitadder_7_s7),
    .S8_COUT(n8bitadder_7_s8_cout), .A0(_1_8_out), .B0(_0_7_out), .in_18(in_1), .in_19(1'b0), .in_20(1'b1),
    .A1(_2_8_out), .B1(_1_7_out), .A2(_3_8_out), .B2(_2_7_out), .A3(_4_8_out), .B3(_3_7_out), .A4(_5_8_out),
    .B4(_4_7_out), .A5(_6_8_out), .B5(_5_7_out), .A6(_7_8_out), .B6(_6_7_out), .A7(1'b0), .B7(_7_7_out));
  and _1_8 (_1_8_out, L_2[0], L[1]);
  and _0_8 (S0, L_2[0], L[0]);

  // Other names for the same wires on the sheet: E = in_1; A0 = L[0]; A1 = L[1]; A2 = L[2]; A3 = L[3]; A4 = L[4];
  //   A5 = L[5]; A6 = L[6]; A7 = L[7]; B0 = L_2[0]; B1 = L_2[1]; B2 = L_2[2]; B3 = L_2[3]; B4 = L_2[4]; B5 = L_2[5];
  //   B6 = L_2[6]; B7 = L_2[7]

  // Notes on the sheet:
  //   M
  //   M
endmodule

module _8bit_adderorSub (
  input  in_1,
  input  Cntrl,
  input  [7:0] in_3,
  input  [7:0] L,
  output S7,
  output S0,
  output S1,
  output S2,
  output S3,
  output S4,
  output S5,
  output S6,
  output out_13,
  output out_14
);

  wire B0, B1, B2, B3, B4, B5, B6, B7, n8bitadder_1_s0, n8bitadder_1_s1, n8bitadder_1_s2, n8bitadder_1_s3,
       n8bitadder_1_s4, n8bitadder_1_s5, n8bitadder_1_s6, n8bitadder_1_s7, not_1_out, xor_9_out, xor_10_out,
       xor_11_out, xor_12_out, xor_13_out, xor_14_out, xor_15_out, xor_16_out;

  _8BITADDER u_8bitadder_1 (
    .CIN(Cntrl), .S0(n8bitadder_1_s0), .S1(n8bitadder_1_s1), .S2(n8bitadder_1_s2), .S3(n8bitadder_1_s3),
    .S4(n8bitadder_1_s4), .S5(n8bitadder_1_s5), .S6(n8bitadder_1_s6), .S7(n8bitadder_1_s7), .S8_COUT(out_14),
    .A0(L[0]), .B0(B0), .in_18(in_1), .in_19(1'b0), .in_20(1'b1), .A1(L[1]), .B1(B1), .A2(L[2]), .B2(B2),
    .A3(L[3]), .B3(B3), .A4(L[4]), .B4(B4), .A5(L[5]), .B5(B5), .A6(L[6]), .B6(B6), .A7(L[7]), .B7(B7));
  not not_1 (not_1_out, out_14);
  xor xor_1 (B0, Cntrl, in_3[0]);
  xor xor_2 (B1, Cntrl, in_3[1]);
  xor xor_3 (B2, in_3[2], Cntrl);
  xor xor_4 (B3, Cntrl, in_3[3]);
  xor xor_5 (B4, in_3[4], Cntrl);
  xor xor_6 (B5, Cntrl, in_3[5]);
  xor xor_7 (B6, Cntrl, in_3[6]);
  xor xor_8 (B7, Cntrl, in_3[7]);
  and and_1 (S7, not_1_out, Cntrl);
  xor xor_9 (xor_9_out, S7, n8bitadder_1_s0);
  xor xor_10 (xor_10_out, n8bitadder_1_s1, S7);
  xor xor_11 (xor_11_out, n8bitadder_1_s2, S7);
  xor xor_12 (xor_12_out, n8bitadder_1_s3, S7);
  xor xor_13 (xor_13_out, n8bitadder_1_s4, S7);
  xor xor_14 (xor_14_out, n8bitadder_1_s5, S7);
  xor xor_15 (xor_15_out, n8bitadder_1_s6, S7);
  xor xor_16 (xor_16_out, n8bitadder_1_s7, S7);
  _8BITADDER u_8bitadder_2 (
    .CIN(S7), .S0(S0), .S1(S1), .S2(S2), .S3(S3), .S4(S4), .S5(S5), .S6(S6), .S7(out_13), .A0(1'b0),
    .B0(xor_9_out), .in_18(in_1), .in_19(1'b0), .in_20(1'b1), .A1(1'b0), .B1(xor_10_out), .A2(1'b0),
    .B2(xor_11_out), .A3(1'b0), .B3(xor_12_out), .A4(1'b0), .B4(xor_13_out), .A5(1'b0), .B5(xor_14_out),
    .A6(1'b0), .B6(xor_15_out), .A7(1'b0), .B7(xor_16_out));  // open: S8_COUT

  // Other names for the same wires on the sheet: E = in_1; A0 = L[0]; A1 = L[1]; A2 = L[2]; A3 = L[3]; A4 = L[4];
  //   A5 = L[5]; A6 = L[6]; A7 = L[7]

  // Notes on the sheet:
  //   8 BIT ADDER /SUB
  //   COUT
  //   SWITCH O FOR ADD 1 FOR SUB
  //   IF A<B RETURN THE ACTUAL WITH SIGN
  //   M
  //   CIN
  //   SIGN  1-VE 0+VE
  //   Carry ONLY FOR ADD
endmodule

// SUBTRACT
module _8bitsubtracter (
  input  in_1,
  input  [7:0] in_2,
  input  [7:0] in_3,
  output D2,
  output D3,
  output D4,
  output D5,
  output D6,
  output D7,
  output COUT,
  output D0,
  output D1
);

  wire B0, B1, B2, B3, B4, B5, B6, B7;

  _8BITADDER u_8bitadder_1 (
    .CIN(1'b1), .S0(D0), .S1(D1), .S2(D2), .S3(D3), .S4(D4), .S5(D5), .S6(D6), .S7(D7), .S8_COUT(COUT),
    .A0(in_3[0]), .B0(B0), .in_18(in_1), .in_19(1'b0), .in_20(1'b1), .A1(in_3[1]), .B1(B1), .A2(in_3[2]),
    .B2(B2), .A3(in_3[3]), .B3(B3), .A4(in_3[4]), .B4(B4), .A5(in_3[5]), .B5(B5), .A6(in_3[6]), .B6(B6),
    .A7(in_3[7]), .B7(B7));
  not not_1 (B0, in_2[0]);
  not not_2 (B1, in_2[1]);
  not not_3 (B2, in_2[2]);
  not not_4 (B3, in_2[3]);
  not not_5 (B4, in_2[4]);
  not not_6 (B5, in_2[5]);
  not not_7 (B6, in_2[6]);
  not not_8 (B7, in_2[7]);

  // Other names for the same wires on the sheet: E = in_1; A0 = in_3[0]; A1 = in_3[1]; A2 = in_3[2]; A3 = in_3[3];
  //   A4 = in_3[4]; A5 = in_3[5]; A6 = in_3[6]; A7 = in_3[7]

  // Notes on the sheet:
  //   8BIT SUBTRACTER(without optimisation)
endmodule

module _8BITDIVIDER (
  input  [7:0] in_1,
  input  [7:0] in_2,
  input  in_3,
  output Q7,
  output Q6,
  output Q5,
  output Q4,
  output Q3,
  output Q2,
  output Q1,
  output R7,
  output R6,
  output out_13,
  output out_14,
  output out_15,
  output R1,
  output out_17,
  output R0,
  output Q0
);

  wire n8bitsubtracter_1_d0, n8bitsubtracter_1_d1, n8bitsubtracter_1_d2, n8bitsubtracter_1_d3,
       n8bitsubtracter_1_d4, n8bitsubtracter_1_d5, n8bitsubtracter_1_d6, n8bitsubtracter_1_d7,
       n8bitsubtracter_2_d0, n8bitsubtracter_2_d1, n8bitsubtracter_2_d2, n8bitsubtracter_2_d3,
       n8bitsubtracter_2_d4, n8bitsubtracter_2_d5, n8bitsubtracter_2_d6, n8bitsubtracter_2_d7,
       n8bitsubtracter_3_d0, n8bitsubtracter_3_d1, n8bitsubtracter_3_d2, n8bitsubtracter_3_d3,
       n8bitsubtracter_3_d4, n8bitsubtracter_3_d5, n8bitsubtracter_3_d6, n8bitsubtracter_3_d7,
       n8bitsubtracter_4_d0, n8bitsubtracter_4_d1, n8bitsubtracter_4_d2, n8bitsubtracter_4_d3,
       n8bitsubtracter_4_d4, n8bitsubtracter_4_d5, n8bitsubtracter_4_d6, n8bitsubtracter_4_d7,
       n8bitsubtracter_5_d0, n8bitsubtracter_5_d1, n8bitsubtracter_5_d2, n8bitsubtracter_5_d3,
       n8bitsubtracter_5_d4, n8bitsubtracter_5_d5, n8bitsubtracter_5_d6, n8bitsubtracter_5_d7,
       n8bitsubtracter_6_d0, n8bitsubtracter_6_d1, n8bitsubtracter_6_d2, n8bitsubtracter_6_d3,
       n8bitsubtracter_6_d4, n8bitsubtracter_6_d5, n8bitsubtracter_6_d6, n8bitsubtracter_6_d7,
       n8bitsubtracter_7_d0, n8bitsubtracter_7_d1, n8bitsubtracter_7_d2, n8bitsubtracter_7_d3,
       n8bitsubtracter_7_d4, n8bitsubtracter_7_d5, n8bitsubtracter_7_d6, n8bitsubtracter_7_d7,
       n8bitsubtracter_8_d0, n8bitsubtracter_8_d1, n8bitsubtracter_8_d2, n8bitsubtracter_8_d3,
       n8bitsubtracter_8_d4, n8bitsubtracter_8_d5, n8bitsubtracter_8_d6, n8bitsubtracter_8_d7;
  wire [7:1] multiplexer_1_out_25, multiplexer_2_out_25, multiplexer_3_out_25, multiplexer_4_out_25,
       multiplexer_5_out_25, multiplexer_6_out_25, multiplexer_7_out_25;

  multiplexer multiplexer_1 (
    .in_17(Q7), .in_1(1'b0), .in_2(1'b0), .B_0(1'b0), .in_4(1'b0), .in_5(1'b0), .in_6(1'b0), .in_7(1'b0),
    .in_8(in_1[7]), .in_9(n8bitsubtracter_1_d7), .in_10(n8bitsubtracter_1_d6), .in_11(n8bitsubtracter_1_d5),
    .in_12(n8bitsubtracter_1_d4), .A_1(n8bitsubtracter_1_d3), .in_14(n8bitsubtracter_1_d2),
    .in_15(n8bitsubtracter_1_d1), .in_16(n8bitsubtracter_1_d0), .out_19(multiplexer_1_out_25[7]),
    .out_20(multiplexer_1_out_25[6]), .out_21(multiplexer_1_out_25[5]), .out_22(multiplexer_1_out_25[4]),
    .out_23(multiplexer_1_out_25[3]), .out_24(multiplexer_1_out_25[2]), .out_25(multiplexer_1_out_25[1]));  // open: out_18
  _8bitsubtracter u_8bitsubtracter_1 (
    .in_3({{7{1'b0}}, in_1[7]}), .in_2(in_2), .D0(n8bitsubtracter_1_d0), .D1(n8bitsubtracter_1_d1),
    .D2(n8bitsubtracter_1_d2), .D3(n8bitsubtracter_1_d3), .D4(n8bitsubtracter_1_d4),
    .D5(n8bitsubtracter_1_d5), .D6(n8bitsubtracter_1_d6), .D7(n8bitsubtracter_1_d7), .COUT(Q7), .in_1(in_3));
  multiplexer multiplexer_2 (
    .in_17(Q6), .in_1(multiplexer_1_out_25[7]), .in_2(multiplexer_1_out_25[6]),
    .B_0(multiplexer_1_out_25[5]), .in_4(multiplexer_1_out_25[4]), .in_5(multiplexer_1_out_25[3]),
    .in_6(multiplexer_1_out_25[2]), .in_7(multiplexer_1_out_25[1]), .in_8(in_1[6]),
    .in_9(n8bitsubtracter_2_d7), .in_10(n8bitsubtracter_2_d6), .in_11(n8bitsubtracter_2_d5),
    .in_12(n8bitsubtracter_2_d4), .A_1(n8bitsubtracter_2_d3), .in_14(n8bitsubtracter_2_d2),
    .in_15(n8bitsubtracter_2_d1), .in_16(n8bitsubtracter_2_d0), .out_19(multiplexer_2_out_25[7]),
    .out_20(multiplexer_2_out_25[6]), .out_21(multiplexer_2_out_25[5]), .out_22(multiplexer_2_out_25[4]),
    .out_23(multiplexer_2_out_25[3]), .out_24(multiplexer_2_out_25[2]), .out_25(multiplexer_2_out_25[1]));  // open: out_18
  multiplexer multiplexer_3 (
    .in_17(Q5), .in_1(multiplexer_2_out_25[7]), .in_2(multiplexer_2_out_25[6]),
    .B_0(multiplexer_2_out_25[5]), .in_4(multiplexer_2_out_25[4]), .in_5(multiplexer_2_out_25[3]),
    .in_6(multiplexer_2_out_25[2]), .in_7(multiplexer_2_out_25[1]), .in_8(in_1[5]),
    .in_9(n8bitsubtracter_3_d7), .in_10(n8bitsubtracter_3_d6), .in_11(n8bitsubtracter_3_d5),
    .in_12(n8bitsubtracter_3_d4), .A_1(n8bitsubtracter_3_d3), .in_14(n8bitsubtracter_3_d2),
    .in_15(n8bitsubtracter_3_d1), .in_16(n8bitsubtracter_3_d0), .out_19(multiplexer_3_out_25[7]),
    .out_20(multiplexer_3_out_25[6]), .out_21(multiplexer_3_out_25[5]), .out_22(multiplexer_3_out_25[4]),
    .out_23(multiplexer_3_out_25[3]), .out_24(multiplexer_3_out_25[2]), .out_25(multiplexer_3_out_25[1]));  // open: out_18
  _8bitsubtracter u_8bitsubtracter_2 (
    .in_3({multiplexer_1_out_25, in_1[6]}), .in_2(in_2), .D0(n8bitsubtracter_2_d0),
    .D1(n8bitsubtracter_2_d1), .D2(n8bitsubtracter_2_d2), .D3(n8bitsubtracter_2_d3),
    .D4(n8bitsubtracter_2_d4), .D5(n8bitsubtracter_2_d5), .D6(n8bitsubtracter_2_d6),
    .D7(n8bitsubtracter_2_d7), .COUT(Q6), .in_1(in_3));
  _8bitsubtracter u_8bitsubtracter_3 (
    .in_3({multiplexer_2_out_25, in_1[5]}), .in_2(in_2), .D0(n8bitsubtracter_3_d0),
    .D1(n8bitsubtracter_3_d1), .D2(n8bitsubtracter_3_d2), .D3(n8bitsubtracter_3_d3),
    .D4(n8bitsubtracter_3_d4), .D5(n8bitsubtracter_3_d5), .D6(n8bitsubtracter_3_d6),
    .D7(n8bitsubtracter_3_d7), .COUT(Q5), .in_1(in_3));
  multiplexer multiplexer_4 (
    .in_17(Q4), .in_1(multiplexer_3_out_25[7]), .in_2(multiplexer_3_out_25[6]),
    .B_0(multiplexer_3_out_25[5]), .in_4(multiplexer_3_out_25[4]), .in_5(multiplexer_3_out_25[3]),
    .in_6(multiplexer_3_out_25[2]), .in_7(multiplexer_3_out_25[1]), .in_8(in_1[4]),
    .in_9(n8bitsubtracter_4_d7), .in_10(n8bitsubtracter_4_d6), .in_11(n8bitsubtracter_4_d5),
    .in_12(n8bitsubtracter_4_d4), .A_1(n8bitsubtracter_4_d3), .in_14(n8bitsubtracter_4_d2),
    .in_15(n8bitsubtracter_4_d1), .in_16(n8bitsubtracter_4_d0), .out_19(multiplexer_4_out_25[7]),
    .out_20(multiplexer_4_out_25[6]), .out_21(multiplexer_4_out_25[5]), .out_22(multiplexer_4_out_25[4]),
    .out_23(multiplexer_4_out_25[3]), .out_24(multiplexer_4_out_25[2]), .out_25(multiplexer_4_out_25[1]));  // open: out_18
  multiplexer multiplexer_5 (
    .in_17(Q3), .in_1(multiplexer_4_out_25[7]), .in_2(multiplexer_4_out_25[6]),
    .B_0(multiplexer_4_out_25[5]), .in_4(multiplexer_4_out_25[4]), .in_5(multiplexer_4_out_25[3]),
    .in_6(multiplexer_4_out_25[2]), .in_7(multiplexer_4_out_25[1]), .in_8(in_1[3]),
    .in_9(n8bitsubtracter_5_d7), .in_10(n8bitsubtracter_5_d6), .in_11(n8bitsubtracter_5_d5),
    .in_12(n8bitsubtracter_5_d4), .A_1(n8bitsubtracter_5_d3), .in_14(n8bitsubtracter_5_d2),
    .in_15(n8bitsubtracter_5_d1), .in_16(n8bitsubtracter_5_d0), .out_19(multiplexer_5_out_25[7]),
    .out_20(multiplexer_5_out_25[6]), .out_21(multiplexer_5_out_25[5]), .out_22(multiplexer_5_out_25[4]),
    .out_23(multiplexer_5_out_25[3]), .out_24(multiplexer_5_out_25[2]), .out_25(multiplexer_5_out_25[1]));  // open: out_18
  _8bitsubtracter u_8bitsubtracter_4 (
    .in_3({multiplexer_3_out_25, in_1[4]}), .in_2(in_2), .D0(n8bitsubtracter_4_d0),
    .D1(n8bitsubtracter_4_d1), .D2(n8bitsubtracter_4_d2), .D3(n8bitsubtracter_4_d3),
    .D4(n8bitsubtracter_4_d4), .D5(n8bitsubtracter_4_d5), .D6(n8bitsubtracter_4_d6),
    .D7(n8bitsubtracter_4_d7), .COUT(Q4), .in_1(in_3));
  _8bitsubtracter u_8bitsubtracter_5 (
    .in_3({multiplexer_4_out_25, in_1[3]}), .in_2(in_2), .D0(n8bitsubtracter_5_d0),
    .D1(n8bitsubtracter_5_d1), .D2(n8bitsubtracter_5_d2), .D3(n8bitsubtracter_5_d3),
    .D4(n8bitsubtracter_5_d4), .D5(n8bitsubtracter_5_d5), .D6(n8bitsubtracter_5_d6),
    .D7(n8bitsubtracter_5_d7), .COUT(Q3), .in_1(in_3));
  multiplexer multiplexer_6 (
    .in_17(Q2), .in_1(multiplexer_5_out_25[7]), .in_2(multiplexer_5_out_25[6]),
    .B_0(multiplexer_5_out_25[5]), .in_4(multiplexer_5_out_25[4]), .in_5(multiplexer_5_out_25[3]),
    .in_6(multiplexer_5_out_25[2]), .in_7(multiplexer_5_out_25[1]), .in_8(in_1[2]),
    .in_9(n8bitsubtracter_6_d7), .in_10(n8bitsubtracter_6_d6), .in_11(n8bitsubtracter_6_d5),
    .in_12(n8bitsubtracter_6_d4), .A_1(n8bitsubtracter_6_d3), .in_14(n8bitsubtracter_6_d2),
    .in_15(n8bitsubtracter_6_d1), .in_16(n8bitsubtracter_6_d0), .out_19(multiplexer_6_out_25[7]),
    .out_20(multiplexer_6_out_25[6]), .out_21(multiplexer_6_out_25[5]), .out_22(multiplexer_6_out_25[4]),
    .out_23(multiplexer_6_out_25[3]), .out_24(multiplexer_6_out_25[2]), .out_25(multiplexer_6_out_25[1]));  // open: out_18
  multiplexer multiplexer_7 (
    .in_17(Q1), .in_1(multiplexer_6_out_25[7]), .in_2(multiplexer_6_out_25[6]),
    .B_0(multiplexer_6_out_25[5]), .in_4(multiplexer_6_out_25[4]), .in_5(multiplexer_6_out_25[3]),
    .in_6(multiplexer_6_out_25[2]), .in_7(multiplexer_6_out_25[1]), .in_8(in_1[1]),
    .in_9(n8bitsubtracter_7_d7), .in_10(n8bitsubtracter_7_d6), .in_11(n8bitsubtracter_7_d5),
    .in_12(n8bitsubtracter_7_d4), .A_1(n8bitsubtracter_7_d3), .in_14(n8bitsubtracter_7_d2),
    .in_15(n8bitsubtracter_7_d1), .in_16(n8bitsubtracter_7_d0), .out_19(multiplexer_7_out_25[7]),
    .out_20(multiplexer_7_out_25[6]), .out_21(multiplexer_7_out_25[5]), .out_22(multiplexer_7_out_25[4]),
    .out_23(multiplexer_7_out_25[3]), .out_24(multiplexer_7_out_25[2]), .out_25(multiplexer_7_out_25[1]));  // open: out_18
  _8bitsubtracter u_8bitsubtracter_6 (
    .in_3({multiplexer_5_out_25, in_1[2]}), .in_2(in_2), .D0(n8bitsubtracter_6_d0),
    .D1(n8bitsubtracter_6_d1), .D2(n8bitsubtracter_6_d2), .D3(n8bitsubtracter_6_d3),
    .D4(n8bitsubtracter_6_d4), .D5(n8bitsubtracter_6_d5), .D6(n8bitsubtracter_6_d6),
    .D7(n8bitsubtracter_6_d7), .COUT(Q2), .in_1(in_3));
  _8bitsubtracter u_8bitsubtracter_7 (
    .in_3({multiplexer_6_out_25, in_1[1]}), .in_2(in_2), .D0(n8bitsubtracter_7_d0),
    .D1(n8bitsubtracter_7_d1), .D2(n8bitsubtracter_7_d2), .D3(n8bitsubtracter_7_d3),
    .D4(n8bitsubtracter_7_d4), .D5(n8bitsubtracter_7_d5), .D6(n8bitsubtracter_7_d6),
    .D7(n8bitsubtracter_7_d7), .COUT(Q1), .in_1(in_3));
  multiplexer multiplexer_8 (
    .in_17(Q0), .in_1(multiplexer_7_out_25[7]), .in_2(multiplexer_7_out_25[6]),
    .B_0(multiplexer_7_out_25[5]), .in_4(multiplexer_7_out_25[4]), .in_5(multiplexer_7_out_25[3]),
    .in_6(multiplexer_7_out_25[2]), .in_7(multiplexer_7_out_25[1]), .in_8(in_1[0]),
    .in_9(n8bitsubtracter_8_d7), .in_10(n8bitsubtracter_8_d6), .in_11(n8bitsubtracter_8_d5),
    .in_12(n8bitsubtracter_8_d4), .A_1(n8bitsubtracter_8_d3), .in_14(n8bitsubtracter_8_d2),
    .in_15(n8bitsubtracter_8_d1), .in_16(n8bitsubtracter_8_d0), .out_18(R7), .out_19(R6), .out_20(out_13),
    .out_21(out_14), .out_22(out_15), .out_23(R1), .out_24(out_17), .out_25(R0));
  _8bitsubtracter u_8bitsubtracter_8 (
    .in_3({multiplexer_7_out_25, in_1[0]}), .in_2(in_2), .D0(n8bitsubtracter_8_d0),
    .D1(n8bitsubtracter_8_d1), .D2(n8bitsubtracter_8_d2), .D3(n8bitsubtracter_8_d3),
    .D4(n8bitsubtracter_8_d4), .D5(n8bitsubtracter_8_d5), .D6(n8bitsubtracter_8_d6),
    .D7(n8bitsubtracter_8_d7), .COUT(Q0), .in_1(in_3));

  // Other names for the same wires on the sheet: A7 = in_1[7]; B0 = in_2[0]; B1 = in_2[1]; B2 = in_2[2]; B3 = in_2[3];
  //   B4 = in_2[4]; B5 = in_2[5]; B6 = in_2[6]; B7 = in_2[7]; A6 = in_1[6]; A5 = in_1[5]; A4 = in_1[4]; A3 = in_1[3];
  //   A2 = in_1[2]; A1 = in_1[1]; A0 = in_1[0]; E = in_3

  // Notes on the sheet:
  //   a
  //   b
  //   s0
  //   a
  //   b
  //   a
  //   s0
  //   b
  //   s0
  //   a
  //   b
  //   a
  //   s0
  //   b
  //   s0
  //   a
  //   b
  //   a
  //   8 BIT DIVISION
  //   s0
  //   b
  //   s0
  //   a
  //   b
  //   s0
endmodule

// MULTIPLEXER
module multiplexer (
  input  in_1,
  input  in_2,
  input  B_0,
  input  in_4,
  input  in_5,
  input  in_6,
  input  in_7,
  input  in_8,
  input  in_9,
  input  in_10,
  input  in_11,
  input  in_12,
  input  A_1,
  input  in_14,
  input  in_15,
  input  in_16,
  input  in_17,
  output out_18,
  output out_19,
  output out_20,
  output out_21,
  output out_22,
  output out_23,
  output out_24,
  output out_25
);

  Multiplexer multiplexer_1 (.in0(in_1), .in1(in_9), .out(out_18), .sel(in_17), .en(1'b1));
  Multiplexer multiplexer_2 (.in0(in_2), .in1(in_10), .out(out_19), .sel(in_17), .en(1'b1));
  Multiplexer multiplexer_3 (.in0(B_0), .in1(in_11), .out(out_20), .sel(in_17), .en(1'b1));
  Multiplexer multiplexer_4 (.in0(in_4), .in1(in_12), .out(out_21), .sel(in_17), .en(1'b1));
  Multiplexer multiplexer_5 (.in0(in_5), .in1(A_1), .out(out_22), .sel(in_17));  // open: en
  Multiplexer multiplexer_6 (.in0(in_7), .in1(in_15), .out(out_24), .sel(in_17), .en(1'b1));
  Multiplexer multiplexer_7 (.in0(in_6), .in1(in_14), .out(out_23), .sel(in_17), .en(1'b1));
  Multiplexer multiplexer_8 (.in0(in_8), .in1(in_16), .out(out_25), .sel(in_17), .en(1'b1));
endmodule

// O/P
module binarytohexa (
  input  [3:0] in_1,
  output out_2,
  output out_3,
  output out_4,
  output out_5,
  output out_6,
  output out_7,
  output out_8
);

  wire decoder_1_out0, decoder_1_out1, decoder_1_out2, decoder_1_out3, decoder_1_out4, decoder_1_out5,
       decoder_1_out6, decoder_1_out7, decoder_1_out8, decoder_1_out9, decoder_1_out10, decoder_1_out11,
       decoder_1_out12, decoder_1_out13, decoder_1_out14, decoder_1_out15;

  Decoder #(.select(4)) decoder_1 (
    .out0(decoder_1_out0), .out1(decoder_1_out1), .out2(decoder_1_out2), .out3(decoder_1_out3),
    .out4(decoder_1_out4), .out5(decoder_1_out5), .out6(decoder_1_out6), .out7(decoder_1_out7),
    .out8(decoder_1_out8), .out9(decoder_1_out9), .out10(decoder_1_out10), .out11(decoder_1_out11),
    .out12(decoder_1_out12), .out13(decoder_1_out13), .out14(decoder_1_out14), .out15(decoder_1_out15),
    .sel(in_1), .en(1'b1));
  or A (out_2, decoder_1_out0, decoder_1_out1, decoder_1_out2, decoder_1_out3, decoder_1_out4, decoder_1_out7, decoder_1_out8, decoder_1_out9, decoder_1_out10, decoder_1_out13);
  or B (out_3, decoder_1_out0, decoder_1_out1, decoder_1_out3, decoder_1_out4, decoder_1_out5, decoder_1_out6, decoder_1_out7, decoder_1_out8, decoder_1_out9, decoder_1_out10, decoder_1_out11, decoder_1_out13);
  or C (out_4, decoder_1_out0, decoder_1_out2, decoder_1_out3, decoder_1_out5, decoder_1_out6, decoder_1_out8, decoder_1_out9, decoder_1_out11, decoder_1_out12, decoder_1_out13, decoder_1_out14);
  or D (out_5, decoder_1_out0, decoder_1_out2, decoder_1_out6, decoder_1_out8, decoder_1_out10, decoder_1_out11, decoder_1_out12, decoder_1_out13, decoder_1_out14, decoder_1_out15);
  or E (out_6, decoder_1_out0, decoder_1_out4, decoder_1_out5, decoder_1_out6, decoder_1_out8, decoder_1_out9, decoder_1_out10, decoder_1_out11, decoder_1_out12, decoder_1_out14, decoder_1_out15);
  or F (out_7, decoder_1_out0, decoder_1_out2, decoder_1_out3, decoder_1_out5, decoder_1_out6, decoder_1_out7, decoder_1_out8, decoder_1_out9, decoder_1_out10, decoder_1_out12, decoder_1_out14, decoder_1_out15);
  or G (out_8, decoder_1_out2, decoder_1_out3, decoder_1_out4, decoder_1_out5, decoder_1_out6, decoder_1_out8, decoder_1_out9, decoder_1_out10, decoder_1_out11, decoder_1_out13, decoder_1_out14, decoder_1_out15);
endmodule

module Calcultor_hex_disp (
  input  [7:0] in_1,
  input  [7:0] in_2,
  input  [1:0] SELECT_LINE,
  output [15:0] A0
);

  wire [8:0] n8bit_adderorsub_2_s0;
  wire [9:0] n8bit_adderorsub_1_s0;
  wire [15:0] n8bitdivider_1_r0, n8bitmultiplier_1_s0;

  _8bitMULTIPLIER u_8bitmultiplier_1 (
    .in_1(1'b1), .L(in_1), .L_2(in_2), .S0(n8bitmultiplier_1_s0[0]), .S1(n8bitmultiplier_1_s0[1]),
    .S2(n8bitmultiplier_1_s0[2]), .S3(n8bitmultiplier_1_s0[3]), .S4(n8bitmultiplier_1_s0[4]),
    .S5(n8bitmultiplier_1_s0[5]), .S6(n8bitmultiplier_1_s0[6]), .S7(n8bitmultiplier_1_s0[7]),
    .S8(n8bitmultiplier_1_s0[8]), .S9(n8bitmultiplier_1_s0[9]), .S10(n8bitmultiplier_1_s0[10]),
    .S11(n8bitmultiplier_1_s0[11]), .S12(n8bitmultiplier_1_s0[12]), .S13(n8bitmultiplier_1_s0[13]),
    .S14(n8bitmultiplier_1_s0[14]), .S15(n8bitmultiplier_1_s0[15]));
  _8BITDIVIDER u_8bitdivider_1 (
    .in_3(1'b1), .in_1(in_1), .in_2(in_2), .Q7(n8bitdivider_1_r0[15]), .Q6(n8bitdivider_1_r0[14]),
    .Q5(n8bitdivider_1_r0[13]), .Q4(n8bitdivider_1_r0[12]), .Q3(n8bitdivider_1_r0[11]),
    .Q2(n8bitdivider_1_r0[10]), .Q1(n8bitdivider_1_r0[9]), .Q0(n8bitdivider_1_r0[8]),
    .R7(n8bitdivider_1_r0[7]), .R6(n8bitdivider_1_r0[6]), .out_13(n8bitdivider_1_r0[5]),
    .out_14(n8bitdivider_1_r0[4]), .out_15(n8bitdivider_1_r0[3]), .R1(n8bitdivider_1_r0[2]),
    .out_17(n8bitdivider_1_r0[1]), .R0(n8bitdivider_1_r0[0]));
  _8bit_adderorSub u_8bit_adderorsub_1 (
    .L(in_1), .in_3(in_2), .Cntrl(1'b0), .S0(n8bit_adderorsub_1_s0[0]), .S1(n8bit_adderorsub_1_s0[1]),
    .S2(n8bit_adderorsub_1_s0[2]), .S3(n8bit_adderorsub_1_s0[3]), .S4(n8bit_adderorsub_1_s0[4]),
    .S5(n8bit_adderorsub_1_s0[5]), .S6(n8bit_adderorsub_1_s0[6]), .out_13(n8bit_adderorsub_1_s0[7]),
    .out_14(n8bit_adderorsub_1_s0[8]), .S7(n8bit_adderorsub_1_s0[9]), .in_1(1'b1));
  _8bit_adderorSub u_8bit_adderorsub_2 (
    .L(in_2), .in_3(in_1), .Cntrl(1'b1), .S0(n8bit_adderorsub_2_s0[0]), .S1(n8bit_adderorsub_2_s0[1]),
    .S2(n8bit_adderorsub_2_s0[2]), .S3(n8bit_adderorsub_2_s0[3]), .S4(n8bit_adderorsub_2_s0[4]),
    .S5(n8bit_adderorsub_2_s0[5]), .S6(n8bit_adderorsub_2_s0[6]), .out_13(n8bit_adderorsub_2_s0[7]),
    .out_14(n8bit_adderorsub_2_s0[8]), .in_1(1'b1));  // open: S7
  Multiplexer #(.select(2), .width(16)) multiplexer_1 (
    .in0({{6{1'b0}}, n8bit_adderorsub_1_s0}), .in1({{7{1'b0}}, n8bit_adderorsub_2_s0}),
    .in2(n8bitmultiplier_1_s0), .in3(n8bitdivider_1_r0), .out(A0), .sel(SELECT_LINE), .en(1'b1));
  Hex_Digit_Display hex_digit_display_1 (.value(A0[15:12]));  // open: dp
  Hex_Digit_Display hex_digit_display_2 (.value(A0[11:8]));  // open: dp
  Hex_Digit_Display hex_digit_display_3 (.value(A0[7:4]));  // open: dp
  Hex_Digit_Display hex_digit_display_4 (.value(A0[3:0]));  // open: dp

  // Other names for the same wires on the sheet: A0_t = in_1[0]; A1 = in_1[1]; A2 = in_1[2]; A3 = in_1[3];
  //   A4 = in_1[4]; A5 = in_1[5]; A6 = in_1[6]; A7 = in_1[7]; B0 = in_2[0]; B1 = in_2[1]; B2 = in_2[2]; B3 = in_2[3];
  //   B4 = in_2[4]; B5 = in_2[5]; B6 = in_2[6]; B7 = in_2[7]

  // Notes on the sheet:
  //   REMAINDER
  //   R0
  //   R7
  //   Q0
  //   Q8
  //   ARITHMETIC CALCULATOR
  //   OUTPUT
  //   A15
  //   DIVISION BY ZERO UNDEFINED
  //   Q
  //   R
  //   Q1
  //   M3
  //   SIGN 1=+VE 0=-VE
  //   SIGN
  //   00 FOR ADD
  //   01 FOR SUBTRACT
  //   Q0
  //   M2
  //   SIGN
  //   CARRY
  //   10 FOR MULTIPLICATION
  //   11 FOR DIVISION
  //   R1
  //   DIV
  //   R0
  //   M1
  //   MUL
  //   M0
  //   D0
  //   SUB
  //   D1
  //   S0
  //   S1
  //   ADD
endmodule
